# Fritzing sketch Telemetria2_0.0.1 (saved by Fritzing 0.9.3b)
circuit board: 4.2356cm x 3.91339cm

parts:
  ESP8266 = ESP8266 WiFi Module [part_number=ESP8266]
  5V_VR = Voltage Regulator [package=78xxl]
  VCC1 = Battery block 9V
  Microcontroller = Arduino Pro Mini v13
  LED1 = RGB LED (com. cathode, rgb) [package="5 mm [THT]"]
  R1 = Resistor [tolerance=±5% resistance=270 package=THT]
  R2 = Resistor [tolerance=±5% resistance=270 package=THT]
  R3 = Resistor [tolerance=±5% resistance=270 package=THT]
  3_3V_VR = V_REG_LD1117VXX [package=78xxl]

nets:
  N1: ESP8266.RXD, Microcontroller.D0/TX
  N2: ESP8266.VCC, 3_3V_VR.OUT
  N3: ESP8266.CH_PD, Microcontroller.D2
  GND: ESP8266.GND, 5V_VR.GND, VCC1.-, Microcontroller.GND, LED1.common_cathode, 3_3V_VR.GND
  N4: ESP8266.TXD, Microcontroller.D1/RX
  N5: 5V_VR.IN, VCC1.+, 3_3V_VR.IN
  N6: 5V_VR.OUT, Microcontroller.VCC
  N7: Microcontroller.D6_PWM, R1.Pin_1
  N8: Microcontroller.D5_PWM, R3.Pin_1
  N9: Microcontroller.D3_PWM, R2.Pin_1
  N10: LED1.red_anode, R2.Pin_0
  N11: LED1.green_anode, R3.Pin_0
  N12: LED1.blue_anode, R1.Pin_0

custom parts:
  ESP8266 WiFi Module: Generic WiFi Module based on the ESP8266 with onboard PCB antenna and UART communications
